# Fritzing sketch ESPStat (saved by Fritzing 0.9.3b)
circuit board: 13.4408cm x 9.82109cm
breadboards: 3

parts:
  IC1 = ULN2803A [package=THT]
  C1 = Ceramic Capacitor [capacitance=0.1mF package="100 mil [THT, multilayer]"]
  REL1 = RELAY [package=relay-jzc]
  REL2 = RELAY [package=relay-jzc]
  REL3 = RELAY [package=relay-jzc]
  REL4 = RELAY [package=relay-jzc]
  DHT1 = DHT22 Humidity and Temperature Sensor
  R1 = Resistor [tolerance=±5% resistance=10k package=THT]
  LED1 = LED - 5mm [color="Green (570nm)" package="5 mm [THT]"]
  R2 = Resistor [tolerance=±5% resistance=150 package=THT]
  M1 = RioRand LM2596
  J1 = screw terminal, 6 pins
  Huzzah_ESP8266 = Adafruit HUZZAH ESP8266 [part_number="Adafruit #2471"]
  IC2 = MCP23017 I2C I/O Expander
  R3 = Resistor [tolerance=±5% resistance=4.7k package=THT]
  LED2 = LED - 3mm [color="Green (570nm)" package="3 mm [THT]"]
  LED3 = LED - 3mm [color="Green (570nm)" package="3 mm [THT]"]
  LED4 = LED - 3mm [color="Green (570nm)" package="3 mm [THT]"]
  LED5 = LED - 3mm [color="Green (570nm)" package="3 mm [THT]"]
  C2 = Ceramic Capacitor [capacitance=100nF package="100 mil [THT, multilayer]"]
  LED6 = LED - 5mm [color="Red (633nm)" package="5 mm [THT]"]
  LED7 = LED - 5mm [color="Red (633nm)" package="5 mm [THT]"]
  LED8 = LED - 5mm [color="Red (633nm)" package="5 mm [THT]"]
  J2 = Screw terminal - 2 pins [package=THT]
  J3 = male pin header, 3 pins [form="♂ (male)"]
  J4 = male pin header, 6 pins [form="♂ (male)"]
  LED9 = LED - 5mm [color="Yellow (595nm)" package="5 mm [THT]"]

nets:
  N1: IC1.In_1, IC2.GPA7
  N2: IC1.In_2, IC2.GPA6
  N3: IC1.In_3, IC2.GPA5
  N4: IC1.In_4, IC2.GPA4
  GND: IC1.0V, C1.1, REL1.COIL1, REL2.COIL1, REL3.COIL1, REL4.COIL1, DHT1.GND, R2.Pin_0, M1.Pin_4, Huzzah_ESP8266.GND, IC2.VSS, IC2.A0, IC2.A1, IC2.A2, LED2.cathode, LED3.cathode, LED4.cathode, LED5.cathode, C2.1, LED6.cathode, LED7.cathode, LED8.cathode, J2.pin2, J4.pin6, LED9.cathode
  N5: IC1.COM_-_Common, C1.0, LED1.anode, Huzzah_ESP8266.VIN, J3.pin2, J4.pin4
  N6: IC1.Out_4, REL4.COIL2
  N7: IC1.Out_3, REL3.COIL2
  N8: IC1.Out_2, REL2.COIL2
  N9: IC1.Out_1, REL1.COIL2
  N10: REL1.NO, J1.pin6
  N11: REL1.MAIN, REL2.MAIN, REL3.MAIN, REL4.MAIN, M1.Pin_1, J1.pin2
  N12: REL2.NO, J1.pin5
  N13: REL3.NO, J1.pin3
  N14: REL4.NO, J1.pin4
  VDD: DHT1.VDD, R1.Pin_0, Huzzah_ESP8266.3.3V, IC2.VDD, C2.0
  N15: DHT1.DATA, R1.Pin_1, Huzzah_ESP8266.GPIO12
  N16: LED1.cathode, R2.Pin_1
  N17: M1.Pin_2, J1.pin1
  N18: M1.Pin_3, J3.pin1
  N19: Huzzah_ESP8266.TX, J4.pin2
  N20: Huzzah_ESP8266.RX, J4.pin3
  N21: Huzzah_ESP8266.GPIO16, LED9.anode
  N22: Huzzah_ESP8266.GPIO14, R3.Pin_1
  N23: Huzzah_ESP8266.GPIO15, LED6.anode
  N24: Huzzah_ESP8266.GPIO2, LED7.anode
  N25: Huzzah_ESP8266.GPIO0, LED8.anode
  N26: Huzzah_ESP8266.GPIO4, IC2.SDA
  N27: Huzzah_ESP8266.GPIO5, IC2.SCL
  N28: IC2.GPB0, LED4.anode
  N29: IC2.GPB1, LED2.anode
  N30: IC2.GPB2, LED3.anode
  N31: IC2.GPB3, LED5.anode
  N32: IC2.GPB7, IC2.GPA0
  N33: IC2.RESET, R3.Pin_0
  N34: J2.pin1, J3.pin3

notes:
  HEAT
  COOL
  FAN ONLY
  CMP
  FAN
  REV
  AUX
  Y
  G
  O
  W
  R
  C
  PWR SELECT
  +
  -
  5V DC @ 1.0A
  PWR
  ESPStat, ESP8266-base IoT smart thermostat for heat pumps, 1.0
  TX
  RX
  +5V
  GND
  RS-232
  NC
  EXT
  COM
  PWR SEL
  EXT +5V DC 1A
  ULN2803A
  MCP23017
  RioRand LM2596 Buck Converter
  C = Common (Blue)
  R = 24VAC (Red)
  O = Reversing Valve (Orange)
  W = AUX/EM Heat (White)
  G = Fan (Green)
  Y = Compressor (Yellow)
  ESPStat Rev 1.0
  Copyright (c) 2021 Cyrus Brunner
  www.cyrusbuilt.net
  FAB 001001 ASSY 001001
  ACT

custom parts:
  Adafruit HUZZAH ESP8266: Add Internet to your next project with an adorable, bite-sized WiFi microcontroller, at a price you like! The ESP8266 processor from Espressif is an 80 MHz microcontroller with a full WiFi front-end (both as client and access point) and TCP/IP stack with DNS support as well. While this chip has been very popular, its also been very difficult to use. Most of the low cost modules are not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
  MCP23017 I2C I/O Expander: The MCP23017 uses two i2c pins (these can be shared with other i2c devices), and in exchange gives you 16 general purpose pins. You can set each of 16 pins to be input, output, input with a pullup or open drain. There's even the ability to get an interrupt via an external pin when any of the inputs change so you don't have to keep polling the chip.
